// Logisim project lcd_de0.circ as structural Verilog: 1 circuit, main circuit main
module main (
  output [7:0] LCD_Data,
  output LCD_RW,
  output LCD_EN,
  output LCD_RS,
  output LCD_BLON,
  output LED_RW,
  output LED_EN,
  output LED_RS,
  output LED_BLON
);

  wire clock_1_out, counter_1_carry, not_1_out;
  wire [2:0] counter_1_q;

  Clock clock_1 (.out(clock_1_out));
  Counter #(.max('h7), .width(3)) counter_1 (
    .clr(1'b0), .load(1'b0), .up(1'b1), .count(not_1_out), .clk(clock_1_out), .D(3'b000),
    .carry(counter_1_carry), .Q(counter_1_q));
  not not_1 (not_1_out, counter_1_carry);
  Multiplexer #(.select(3), .width(10)) multiplexer_1 (
    .in0(10'h30), .in1(10'h8), .in2(10'h1), .in3(10'h6), .in4(10'hf), .in5(10'h80), .in7(10'h383),
    .out({LCD_RS, LCD_RW, LCD_Data}), .sel(counter_1_q));  // open: in6
  Hex_Digit_Display Hex_Digit_Display_1 (.value(LCD_Data[7:4]));  // open: dp
  Hex_Digit_Display Hex_Digit_Display_2 (.value(LCD_Data[3:0]));  // open: dp

  assign LCD_BLON = 1'b1;
  assign LCD_EN = 1'b1;
  assign LED_BLON = 1'b1;
  assign LED_EN = 1'b1;
  assign LED_RS = LCD_RS;
  assign LED_RW = LCD_RW;
endmodule
