// Logisim project slqisc.circ as structural Verilog: 1 circuit, main circuit main
module main (
);

  wire and_1_out, buffer_1_out, buffer_2_out, buffer_3_out, buffer_4_out, buffer_5_out, buffer_6_out,
       buffer_7_out, buffer_8_out, buffer_9_out, buffer_10_out, buffer_11_out, clock_1_out, comparator_1_gt,
       comparator_2_eq, decoder_1_out0, decoder_1_out1, decoder_1_out2, decoder_1_out3, decoder_1_out4,
       decoder_1_out5, decoder_1_out6, decoder_2_out0, decoder_2_out1, decoder_2_out2, decoder_2_out3,
       decoder_2_out4, decoder_2_out5, decoder_2_out6, decoder_2_out7, decoder_2_out8, decoder_2_out9,
       decoder_2_out10, decoder_2_out11, decoder_2_out12, decoder_2_out13, decoder_2_out14, decoder_2_out15,
       decoder_3_out0, decoder_3_out1, decoder_3_out2, decoder_3_out3, decoder_3_out4, decoder_3_out5,
       decoder_3_out6, decoder_3_out7, decoder_3_out8, decoder_3_out9, decoder_3_out10, decoder_3_out11,
       decoder_3_out12, decoder_3_out13, decoder_3_out14, decoder_3_out15;
  wire [2:0] counter_1_q;
  wire [3:0] counter_2_q;
  wire [6:0] Sub_q;
  wire [15:0] adder_1_out, adder_2_out, adder_3_out, adder_4_out, Adr_q, Min_q, MinLoc_q, multiplexer_1_out,
       multiplexer_2_out, negator_1_out, PC_q, ram_1_dout, SubLoc_q;
  wire [15:7] Sub_q_2;
  wire [24:0] register_1_q, register_2_q, register_3_q, register_4_q, register_5_q, register_6_q,
       register_7_q, register_8_q, register_9_q, register_10_q, register_11_q, register_12_q, register_13_q,
       register_14_q, register_15_q, register_16_q, rom_1_data;

  Clock clock_1 (.out(clock_1_out));
  Multiplexer #(.width(16)) multiplexer_1 (
    .in0(Adr_q), .in1(adder_3_out), .out(multiplexer_1_out), .sel(comparator_1_gt));
  Comparator #(.width(16)) comparator_1 (.a(adder_4_out), .b({16{1'b0}}), .gt(comparator_1_gt));  // open: eq, lt
  Register #(.width(16)) PC (.D(multiplexer_1_out), .en(decoder_1_out6), .clk(buffer_1_out), .Q(PC_q));  // open: clr
  buf buffer_1 (buffer_1_out, clock_1_out);
  Counter #(.max('h7), .width(3)) counter_1 (
    .up(1'b1), .clk(clock_1_out), .Q(counter_1_q));  // open: clr, load, count, D, carry
  buf buffer_2 (buffer_2_out, clock_1_out);
  Adder #(.width(16)) adder_1 (.a(PC_q), .b(16'h1), .out(adder_1_out));  // open: cin, cout
  Adder #(.width(16)) adder_2 (.a(PC_q), .b(16'h2), .out(adder_2_out));  // open: cin, cout
  Adder #(.width(16)) adder_3 (.a(PC_q), .b(16'h3), .out(adder_3_out));  // open: cin, cout
  buf buffer_3 (buffer_3_out, buffer_2_out);
  buf buffer_4 (buffer_4_out, buffer_3_out);
  Multiplexer #(.select(3), .width(16)) multiplexer_2 (
    .in0(PC_q), .in1(adder_1_out), .in2(adder_2_out), .in3(SubLoc_q), .in4(MinLoc_q), .in5(MinLoc_q),
    .out(multiplexer_2_out), .sel(counter_1_q));  // open: in6, in7
  RAM #(.addrWidth(16), .dataWidth(16), .\type ("nonvolatile")) ram_1 (
    .addr(multiplexer_2_out), .we(decoder_1_out5), .oe(1'b1), .clk(clock_1_out), .din(adder_4_out),
    .dout(ram_1_dout));
  buf buffer_5 (buffer_5_out, buffer_4_out);
  buf buffer_6 (buffer_6_out, buffer_5_out);
  buf buffer_7 (buffer_7_out, buffer_6_out);
  buf buffer_8 (buffer_8_out, buffer_7_out);
  buf buffer_9 (buffer_9_out, buffer_8_out);
  buf buffer_10 (buffer_10_out, buffer_9_out);
  buf buffer_11 (buffer_11_out, buffer_10_out);
  Decoder #(.enable("false"), .select(3)) decoder_1 (
    .out0(decoder_1_out0), .out1(decoder_1_out1), .out2(decoder_1_out2), .out3(decoder_1_out3),
    .out4(decoder_1_out4), .out5(decoder_1_out5), .out6(decoder_1_out6), .sel(counter_1_q));  // open: out7
  Register #(.width(16)) SubLoc (.D(ram_1_dout), .en(decoder_1_out0), .clk(buffer_11_out), .Q(SubLoc_q));  // open: clr
  Register #(.width(16)) MinLoc (.D(ram_1_dout), .en(decoder_1_out1), .clk(buffer_11_out), .Q(MinLoc_q));  // open: clr
  Register #(.width(16)) Adr (.D(ram_1_dout), .en(decoder_1_out2), .clk(buffer_11_out), .Q(Adr_q));  // open: clr
  Register #(.width(16)) Sub (
    .D(ram_1_dout), .en(decoder_1_out3), .clk(buffer_11_out), .Q({Sub_q_2, Sub_q}));  // open: clr
  Register #(.width(16)) Min (.D(ram_1_dout), .en(decoder_1_out4), .clk(buffer_11_out), .Q(Min_q));  // open: clr
  Comparator #(.width(16)) comparator_2 (.a(MinLoc_q), .b({16{1'b1}}), .eq(comparator_2_eq));  // open: gt, lt
  Negator #(.width(16)) negator_1 (.in({Sub_q_2, Sub_q}), .out(negator_1_out));
  Adder #(.width(16)) adder_4 (.a(negator_1_out), .b(Min_q), .out(adder_4_out));  // open: cin, cout
  and and_1 (and_1_out, decoder_1_out6, comparator_2_eq);
  ROM #(.addrWidth(7), .dataWidth(25)) rom_1 (.addr(Sub_q), .data(rom_1_data));
  Register #(.width(25)) register_1 (
    .D(rom_1_data), .en(decoder_2_out0), .clk(buffer_11_out), .Q(register_1_q));  // open: clr
  Register #(.width(25)) register_2 (
    .D(rom_1_data), .en(decoder_2_out1), .clk(buffer_11_out), .Q(register_2_q));  // open: clr
  Decoder #(.select(4)) decoder_2 (
    .out0(decoder_2_out0), .out1(decoder_2_out1), .out2(decoder_2_out2), .out3(decoder_2_out3),
    .out4(decoder_2_out4), .out5(decoder_2_out5), .out6(decoder_2_out6), .out7(decoder_2_out7),
    .out8(decoder_2_out8), .out9(decoder_2_out9), .out10(decoder_2_out10), .out11(decoder_2_out11),
    .out12(decoder_2_out12), .out13(decoder_2_out13), .out14(decoder_2_out14), .out15(decoder_2_out15),
    .sel(counter_2_q), .en(and_1_out));
  Counter #(.max('hf), .width(4)) counter_2 (
    .up(1'b1), .count(and_1_out), .clk(buffer_11_out), .Q(counter_2_q));  // open: clr, load, D, carry
  LED led_1 (.in(decoder_3_out0));
  DotMatrix #(.matrixrows(5)) dotmatrix_1 (
    .col0(register_1_q[24:20]), .col1(register_1_q[19:15]), .col2(register_1_q[14:10]),
    .col3(register_1_q[9:5]), .col4(register_1_q[4:0]));
  Register #(.width(25)) register_3 (
    .D(rom_1_data), .en(decoder_2_out2), .clk(buffer_11_out), .Q(register_3_q));  // open: clr
  LED led_2 (.in(decoder_3_out1));
  DotMatrix #(.matrixrows(5)) dotmatrix_2 (
    .col0(register_2_q[24:20]), .col1(register_2_q[19:15]), .col2(register_2_q[14:10]),
    .col3(register_2_q[9:5]), .col4(register_2_q[4:0]));
  DotMatrix #(.matrixrows(5)) dotmatrix_3 (
    .col0(register_3_q[24:20]), .col1(register_3_q[19:15]), .col2(register_3_q[14:10]),
    .col3(register_3_q[9:5]), .col4(register_3_q[4:0]));
  Register #(.width(25)) register_4 (
    .D(rom_1_data), .en(decoder_2_out3), .clk(buffer_11_out), .Q(register_4_q));  // open: clr
  LED led_3 (.in(decoder_3_out2));
  LED led_4 (.in(decoder_3_out3));
  DotMatrix #(.matrixrows(5)) dotmatrix_4 (
    .col0(register_4_q[24:20]), .col1(register_4_q[19:15]), .col2(register_4_q[14:10]),
    .col3(register_4_q[9:5]), .col4(register_4_q[4:0]));
  Register #(.width(25)) register_5 (
    .D(rom_1_data), .en(decoder_2_out4), .clk(buffer_11_out), .Q(register_5_q));  // open: clr
  Register #(.width(25)) register_6 (
    .D(rom_1_data), .en(decoder_2_out5), .clk(buffer_11_out), .Q(register_6_q));  // open: clr
  LED led_5 (.in(decoder_3_out4));
  DotMatrix #(.matrixrows(5)) dotmatrix_5 (
    .col0(register_5_q[24:20]), .col1(register_5_q[19:15]), .col2(register_5_q[14:10]),
    .col3(register_5_q[9:5]), .col4(register_5_q[4:0]));
  Register #(.width(25)) register_7 (
    .D(rom_1_data), .en(decoder_2_out6), .clk(buffer_11_out), .Q(register_7_q));  // open: clr
  LED led_6 (.in(decoder_3_out5));
  DotMatrix #(.matrixrows(5)) dotmatrix_6 (
    .col0(register_6_q[24:20]), .col1(register_6_q[19:15]), .col2(register_6_q[14:10]),
    .col3(register_6_q[9:5]), .col4(register_6_q[4:0]));
  DotMatrix #(.matrixrows(5)) dotmatrix_7 (
    .col0(register_7_q[24:20]), .col1(register_7_q[19:15]), .col2(register_7_q[14:10]),
    .col3(register_7_q[9:5]), .col4(register_7_q[4:0]));
  Register #(.width(25)) register_8 (
    .D(rom_1_data), .en(decoder_2_out7), .clk(buffer_11_out), .Q(register_8_q));  // open: clr
  Decoder #(.enable("false"), .select(4)) decoder_3 (
    .out0(decoder_3_out0), .out1(decoder_3_out1), .out2(decoder_3_out2), .out3(decoder_3_out3),
    .out4(decoder_3_out4), .out5(decoder_3_out5), .out6(decoder_3_out6), .out7(decoder_3_out7),
    .out8(decoder_3_out8), .out9(decoder_3_out9), .out10(decoder_3_out10), .out11(decoder_3_out11),
    .out12(decoder_3_out12), .out13(decoder_3_out13), .out14(decoder_3_out14), .out15(decoder_3_out15),
    .sel(counter_2_q));
  LED led_7 (.in(decoder_3_out6));
  LED led_8 (.in(decoder_3_out7));
  DotMatrix #(.matrixrows(5)) dotmatrix_8 (
    .col0(register_8_q[24:20]), .col1(register_8_q[19:15]), .col2(register_8_q[14:10]),
    .col3(register_8_q[9:5]), .col4(register_8_q[4:0]));
  Register #(.width(25)) register_9 (
    .D(rom_1_data), .en(decoder_2_out8), .clk(buffer_11_out), .Q(register_9_q));  // open: clr
  Register #(.width(25)) register_10 (
    .D(rom_1_data), .en(decoder_2_out9), .clk(buffer_11_out), .Q(register_10_q));  // open: clr
  LED led_9 (.in(decoder_3_out8));
  DotMatrix #(.matrixrows(5)) dotmatrix_9 (
    .col0(register_9_q[24:20]), .col1(register_9_q[19:15]), .col2(register_9_q[14:10]),
    .col3(register_9_q[9:5]), .col4(register_9_q[4:0]));
  Register #(.width(25)) register_11 (
    .D(rom_1_data), .en(decoder_2_out10), .clk(buffer_11_out), .Q(register_11_q));  // open: clr
  LED led_10 (.in(decoder_3_out9));
  DotMatrix #(.matrixrows(5)) dotmatrix_10 (
    .col0(register_10_q[24:20]), .col1(register_10_q[19:15]), .col2(register_10_q[14:10]),
    .col3(register_10_q[9:5]), .col4(register_10_q[4:0]));
  DotMatrix #(.matrixrows(5)) dotmatrix_11 (
    .col0(register_11_q[24:20]), .col1(register_11_q[19:15]), .col2(register_11_q[14:10]),
    .col3(register_11_q[9:5]), .col4(register_11_q[4:0]));
  Register #(.width(25)) register_12 (
    .D(rom_1_data), .en(decoder_2_out11), .clk(buffer_11_out), .Q(register_12_q));  // open: clr
  LED led_11 (.in(decoder_3_out10));
  LED led_12 (.in(decoder_3_out11));
  DotMatrix #(.matrixrows(5)) dotmatrix_12 (
    .col0(register_12_q[24:20]), .col1(register_12_q[19:15]), .col2(register_12_q[14:10]),
    .col3(register_12_q[9:5]), .col4(register_12_q[4:0]));
  Register #(.width(25)) register_13 (
    .D(rom_1_data), .en(decoder_2_out12), .clk(buffer_11_out), .Q(register_13_q));  // open: clr
  Register #(.width(25)) register_14 (
    .D(rom_1_data), .en(decoder_2_out13), .clk(buffer_11_out), .Q(register_14_q));  // open: clr
  LED led_13 (.in(decoder_3_out12));
  DotMatrix #(.matrixrows(5)) dotmatrix_13 (
    .col0(register_13_q[24:20]), .col1(register_13_q[19:15]), .col2(register_13_q[14:10]),
    .col3(register_13_q[9:5]), .col4(register_13_q[4:0]));
  Register #(.width(25)) register_15 (
    .D(rom_1_data), .en(decoder_2_out14), .clk(buffer_11_out), .Q(register_15_q));  // open: clr
  LED led_14 (.in(decoder_3_out13));
  DotMatrix #(.matrixrows(5)) dotmatrix_14 (
    .col0(register_14_q[24:20]), .col1(register_14_q[19:15]), .col2(register_14_q[14:10]),
    .col3(register_14_q[9:5]), .col4(register_14_q[4:0]));
  DotMatrix #(.matrixrows(5)) dotmatrix_15 (
    .col0(register_15_q[24:20]), .col1(register_15_q[19:15]), .col2(register_15_q[14:10]),
    .col3(register_15_q[9:5]), .col4(register_15_q[4:0]));
  Register #(.width(25)) register_16 (
    .D(rom_1_data), .en(decoder_2_out15), .clk(buffer_11_out), .Q(register_16_q));  // open: clr
  LED led_15 (.in(decoder_3_out14));
  LED led_16 (.in(decoder_3_out15));
  DotMatrix #(.matrixrows(5)) dotmatrix_16 (
    .col0(register_16_q[24:20]), .col1(register_16_q[19:15]), .col2(register_16_q[14:10]),
    .col3(register_16_q[9:5]), .col4(register_16_q[4:0]));

  // Notes on the sheet:
  //   contents of rom_1 (hex, n*v repeats v):
  //   0 1fa529f 1fad6bb 1f8c631 1f8c62e 1fad6b5 1fa5294 1f8d6b7 1f2109f 7c00 70843f 1f21151 1f08421
  //   1f4111f 1f4105f 1f8c63f 1fa529c 1f8d67f 1fa52dd 1dad6b7 1087e10 1f0843f 1c1045c 1f1105f 1151151
  //   1c21c9c 119d731 7400 e8d62e 447c00 99d6a9 a8d6aa 4653e4 1dad6b2 ead6a2 1085f10 aad6aa 8ad6ae 2ad6ae
  //   1f294a2 e8c631 2294bf ead6ac fa5208 8ad6be 1f21083 5c00 208436 7c45
endmodule
