// Logisim project slqisc_de0.circ as structural Verilog: 1 circuit, main circuit main
module main (
);

  wire and_1_out, buffer_1_out, buffer_2_out, buffer_3_out, buffer_4_out, buffer_5_out, buffer_6_out,
       buffer_7_out, buffer_8_out, buffer_9_out, buffer_10_out, buffer_11_out, clock_1_out, comparator_1_gt,
       comparator_2_eq, decoder_1_out0, decoder_1_out1, decoder_1_out2, decoder_1_out3, decoder_1_out4,
       decoder_1_out5, decoder_1_out6, decoder_1_out7, decoder_2_out0, decoder_2_out1, decoder_2_out2,
       decoder_2_out3, decoder_2_out4, decoder_2_out5, decoder_2_out6;
  wire [2:0] counter_1_q;
  wire [3:0] register_1_q_2;
  wire [11:0] register_1_q;
  wire [15:0] adder_1_out, adder_2_out, adder_3_out, adder_4_out, Adr_q, Min_q, MinLoc_q, multiplexer_1_out,
       multiplexer_2_out, negator_1_out, PC_q, RAM_1_dout, Sub_q, SubLoc_q;

  Clock clock_1 (.out(clock_1_out));
  Multiplexer #(.width(16)) multiplexer_1 (
    .in0(Adr_q), .in1(adder_3_out), .out(multiplexer_1_out), .sel(comparator_1_gt));
  Comparator #(.width(16)) comparator_1 (.a(adder_4_out), .b({16{1'b0}}), .gt(comparator_1_gt));  // open: eq, lt
  Register #(.width(16)) PC (.D(multiplexer_1_out), .en(decoder_2_out6), .clk(buffer_1_out), .Q(PC_q));  // open: clr
  buf buffer_1 (buffer_1_out, clock_1_out);
  Counter #(.max('h7), .width(3)) counter_1 (
    .up(1'b1), .clk(clock_1_out), .Q(counter_1_q));  // open: clr, load, count, D, carry
  buf buffer_2 (buffer_2_out, clock_1_out);
  Adder #(.width(16)) adder_1 (.a(PC_q), .b(16'h1), .out(adder_1_out));  // open: cin, cout
  Adder #(.width(16)) adder_2 (.a(PC_q), .b(16'h2), .out(adder_2_out));  // open: cin, cout
  Adder #(.width(16)) adder_3 (.a(PC_q), .b(16'h3), .out(adder_3_out));  // open: cin, cout
  buf buffer_3 (buffer_3_out, buffer_2_out);
  buf buffer_4 (buffer_4_out, buffer_3_out);
  Multiplexer #(.select(3), .width(16)) multiplexer_2 (
    .in0(PC_q), .in1(adder_1_out), .in2(adder_2_out), .in3(SubLoc_q), .in4(MinLoc_q), .in5(MinLoc_q),
    .out(multiplexer_2_out), .sel(counter_1_q));  // open: in6, in7
  RAM #(.addrWidth(14), .dataWidth(16)) RAM_1 (
    .addr(multiplexer_2_out[13:0]), .we(decoder_2_out5), .oe(1'b1), .clk(clock_1_out), .din(adder_4_out),
    .dout(RAM_1_dout));
  Decoder #(.enable("false"), .select(3)) decoder_1 (
    .out0(decoder_1_out0), .out1(decoder_1_out1), .out2(decoder_1_out2), .out3(decoder_1_out3),
    .out4(decoder_1_out4), .out5(decoder_1_out5), .out6(decoder_1_out6), .out7(decoder_1_out7),
    .sel(counter_1_q));
  LED LED_1 (.in(decoder_1_out0));
  LED LED_2 (.in(decoder_1_out1));
  LED LED_3 (.in(decoder_1_out2));
  buf buffer_5 (buffer_5_out, buffer_4_out);
  buf buffer_6 (buffer_6_out, buffer_5_out);
  buf buffer_7 (buffer_7_out, buffer_6_out);
  LED LED_4 (.in(decoder_1_out3));
  LED LED_5 (.in(decoder_1_out4));
  LED LED_6 (.in(decoder_1_out5));
  LED LED_7 (.in(decoder_1_out6));
  buf buffer_8 (buffer_8_out, buffer_7_out);
  buf buffer_9 (buffer_9_out, buffer_8_out);
  buf buffer_10 (buffer_10_out, buffer_9_out);
  LED LED_8 (.in(decoder_1_out7));
  buf buffer_11 (buffer_11_out, buffer_10_out);
  Decoder #(.enable("false"), .select(3)) decoder_2 (
    .out0(decoder_2_out0), .out1(decoder_2_out1), .out2(decoder_2_out2), .out3(decoder_2_out3),
    .out4(decoder_2_out4), .out5(decoder_2_out5), .out6(decoder_2_out6), .sel(counter_1_q));  // open: out7
  Register #(.width(16)) SubLoc (.D(RAM_1_dout), .en(decoder_2_out0), .clk(buffer_11_out), .Q(SubLoc_q));  // open: clr
  Register #(.width(16)) MinLoc (.D(RAM_1_dout), .en(decoder_2_out1), .clk(buffer_11_out), .Q(MinLoc_q));  // open: clr
  Register #(.width(16)) Adr (.D(RAM_1_dout), .en(decoder_2_out2), .clk(buffer_11_out), .Q(Adr_q));  // open: clr
  Register #(.width(16)) Sub (.D(RAM_1_dout), .en(decoder_2_out3), .clk(buffer_11_out), .Q(Sub_q));  // open: clr
  Register #(.width(16)) Min (.D(RAM_1_dout), .en(decoder_2_out4), .clk(buffer_11_out), .Q(Min_q));  // open: clr
  Comparator #(.width(16)) comparator_2 (.a(MinLoc_q), .b({16{1'b1}}), .eq(comparator_2_eq));  // open: gt, lt
  Negator #(.width(16)) negator_1 (.in(Sub_q), .out(negator_1_out));
  Adder #(.width(16)) adder_4 (.a(negator_1_out), .b(Min_q), .out(adder_4_out));  // open: cin, cout
  and and_1 (and_1_out, decoder_2_out6, comparator_2_eq);
  Register #(.width(16)) register_1 (
    .D(Sub_q), .en(and_1_out), .clk(buffer_11_out), .Q({register_1_q_2, register_1_q}));  // open: clr
  Hex_Digit_Display Hex_Digit_Display_1 (.value(register_1_q_2));  // open: dp
  Hex_Digit_Display Hex_Digit_Display_2 (.value(register_1_q[11:8]));  // open: dp
  Hex_Digit_Display Hex_Digit_Display_3 (.value(register_1_q[7:4]));  // open: dp
  Hex_Digit_Display Hex_Digit_Display_4 (.value(register_1_q[3:0]));  // open: dp
endmodule
