// Logisim project slqisc_flash_de0.circ as structural Verilog: 1 circuit, main circuit main
module main (
);

  wire and_1_out, clock_1_out, comparator_1_gt, comparator_2_eq, counter_1_carry, decoder_1_out0,
       decoder_1_out1, decoder_1_out2, decoder_1_out3, decoder_1_out4, decoder_1_out5, decoder_1_out6,
       decoder_1_out7, decoder_2_out1, decoder_2_out2, decoder_2_out3, decoder_2_out4, decoder_2_out5,
       decoder_2_out6, decoder_2_out7, not_1_out, or_1_out, RESET_out;
  wire [2:0] counter_2_q;
  wire [3:0] register_1_q_2;
  wire [11:0] register_1_q;
  wire [13:0] counter_1_q, multiplexer_3_out;
  wire [15:0] adder_1_out, adder_2_out, adder_3_out, Adr_q, bit_extender_1_out, Min_q, MinLoc_q,
       multiplexer_1_out, multiplexer_2_out, multiplexer_4_out, negator_1_out, PC_q, RAM_1_dout, ROM_1_data,
       Sub_q, SubLoc_q;

  Clock clock_1 (.out(clock_1_out));
  Multiplexer #(.width(16)) multiplexer_1 (
    .in0(Adr_q), .in1(adder_2_out), .out(multiplexer_1_out), .sel(comparator_1_gt));
  Comparator #(.width(16)) comparator_1 (.a(adder_3_out), .b({16{1'b0}}), .gt(comparator_1_gt));  // open: eq, lt
  Counter #(.max('h3fff), .ongoal("stay"), .width(14)) counter_1 (
    .clr(RESET_out), .load(1'b0), .up(1'b1), .count(not_1_out), .clk(clock_1_out), .D({14{1'b1}}),
    .carry(counter_1_carry), .Q(counter_1_q));
  Register #(.width(16)) PC (.D(multiplexer_1_out), .en(decoder_2_out7), .clk(clock_1_out), .Q(PC_q), .clr(RESET_out));
  not not_1 (not_1_out, counter_1_carry);
  assign bit_extender_1_out = {{13{1'b0}}, counter_2_q};  // Bit_Extender bit_extender_1
  Counter #(.max('h7), .width(3)) counter_2 (
    .clr(RESET_out), .load(not_1_out), .up(1'b1), .count(counter_1_carry), .clk(clock_1_out), .D(3'b111),
    .Q(counter_2_q));  // open: carry
  ROM #(.addrWidth(14), .dataWidth(16)) ROM_1 (.addr(counter_1_q), .data(ROM_1_data));
  Adder #(.width(16)) adder_1 (.a(PC_q), .b(bit_extender_1_out), .out(adder_1_out));  // open: cin, cout
  Adder #(.width(16)) adder_2 (.a(PC_q), .b(16'h3), .out(adder_2_out));  // open: cin, cout
  Multiplexer #(.select(3), .width(16)) multiplexer_2 (
    .in0(adder_1_out), .in1(adder_1_out), .in2(adder_1_out), .in3(SubLoc_q), .in4(MinLoc_q), .in5(MinLoc_q),
    .in6(MinLoc_q), .out(multiplexer_2_out), .sel(counter_2_q));  // open: in7
  Multiplexer #(.width(14)) multiplexer_3 (
    .in0(counter_1_q), .in1(multiplexer_2_out[13:0]), .out(multiplexer_3_out), .sel(counter_1_carry));
  Multiplexer #(.width(16)) multiplexer_4 (
    .in0(ROM_1_data), .in1(adder_3_out), .out(multiplexer_4_out), .sel(counter_1_carry));
  or or_1 (or_1_out, ~counter_1_carry, decoder_2_out6);  // OR_Gate
  RAM #(.addrWidth(14), .dataWidth(16), .\type ("nonvolatile")) RAM_1 (
    .addr(multiplexer_3_out), .we(or_1_out), .oe(counter_1_carry), .clk(clock_1_out),
    .din(multiplexer_4_out), .dout(RAM_1_dout));
  LED LED_1 (.in(decoder_1_out0));
  LED LED_2 (.in(decoder_1_out1));
  Button RESET (.out(RESET_out));
  Decoder #(.enable("false"), .select(3)) decoder_1 (
    .out0(decoder_1_out0), .out1(decoder_1_out1), .out2(decoder_1_out2), .out3(decoder_1_out3),
    .out4(decoder_1_out4), .out5(decoder_1_out5), .out6(decoder_1_out6), .out7(decoder_1_out7),
    .sel(counter_2_q));
  LED LED_3 (.in(decoder_1_out2));
  LED LED_4 (.in(decoder_1_out3));
  LED LED_5 (.in(decoder_1_out4));
  LED LED_6 (.in(decoder_1_out5));
  LED LED_7 (.in(decoder_1_out6));
  LED LED_8 (.in(decoder_1_out7));
  Decoder #(.enable("false"), .select(3)) decoder_2 (
    .out1(decoder_2_out1), .out2(decoder_2_out2), .out3(decoder_2_out3), .out4(decoder_2_out4),
    .out5(decoder_2_out5), .out6(decoder_2_out6), .out7(decoder_2_out7), .sel(counter_2_q));  // open: out0
  Register #(.trigger("falling"), .width(16)) SubLoc (
    .D(RAM_1_dout), .en(decoder_2_out1), .clk(clock_1_out), .Q(SubLoc_q), .clr(RESET_out));
  Register #(.trigger("falling"), .width(16)) MinLoc (
    .D(RAM_1_dout), .en(decoder_2_out2), .clk(clock_1_out), .Q(MinLoc_q), .clr(RESET_out));
  Register #(.trigger("falling"), .width(16)) Adr (
    .D(RAM_1_dout), .en(decoder_2_out3), .clk(clock_1_out), .Q(Adr_q), .clr(RESET_out));
  Register #(.trigger("falling"), .width(16)) Sub (
    .D(RAM_1_dout), .en(decoder_2_out4), .clk(clock_1_out), .Q(Sub_q), .clr(RESET_out));
  Register #(.trigger("falling"), .width(16)) Min (
    .D(RAM_1_dout), .en(decoder_2_out5), .clk(clock_1_out), .Q(Min_q), .clr(RESET_out));
  Comparator #(.width(16)) comparator_2 (.a(MinLoc_q), .b({16{1'b1}}), .eq(comparator_2_eq));  // open: gt, lt
  Negator #(.width(16)) negator_1 (.in(Sub_q), .out(negator_1_out));
  Adder #(.width(16)) adder_3 (.a(negator_1_out), .b(Min_q), .out(adder_3_out));  // open: cin, cout
  and and_1 (and_1_out, comparator_2_eq, decoder_2_out7);
  Register #(.trigger("falling"), .width(16)) register_1 (
    .D(Sub_q), .en(and_1_out), .clk(clock_1_out), .Q({register_1_q_2, register_1_q}), .clr(RESET_out));
  Hex_Digit_Display Hex_Digit_Display_1 (.value(register_1_q_2));  // open: dp
  Hex_Digit_Display Hex_Digit_Display_2 (.value(register_1_q[11:8]));  // open: dp
  Hex_Digit_Display Hex_Digit_Display_3 (.value(register_1_q[7:4]));  // open: dp
  Hex_Digit_Display Hex_Digit_Display_4 (.value(register_1_q[3:0]));  // open: dp

  // Notes on the sheet:
  //   contents of ROM_1 (hex, n*v repeats v):
  //   ffef ffef 3 2b2 2a9 6 2a9 ffef 9 2a9 2a9 c f f 10 0 2aa ffef 13 2aa f 16 2ab ffef 1c 2a9 2a9 13 ffef
  //   ffef 1f f 2a9 22 2a9 ffef 25 2a9 2a9 28 2ac ffef 2b ffee ffee 2e 2b2 2a9 31 2a9 ffee 34 2a9 2a9 37
  //   ffeb ffeb 3a ffef 2a9 3d 2a9 ffeb 40 2a9 2a9 43 ffeb 2a9 46 2a9 ffeb 49 2a9 2a9 4c ffeb 2a9 4f 2a9
  //   ffeb 52 2a9 2a9 55 ffeb 2a9 58 2a9 ffeb 5b 2a9 2a9 5e 65 65 61 64 64 66 0 0 2ad 2a9 69 2a9 64 7b 2a9
  //   2a9 6f 2ac 64 72 ffeb 2a9 75 2a9 65 78 2a9 2a9 69 ffeb ffeb 7e 65 2a9 81 2a9 ffeb 84 2a9 2a9 87 ffeb
  //   ffee 8a 8d 8d 8e 0 2aa ffee 91 2aa 8d 94 2ae ffee 9a 2a9 2a9 91 ffee ffee 9d 8d 2a9 a0 2a9 ffee a3
  //   2a9 2a9 a6 2ac ffee a9 ffed ffed ac 2b2 2a9 af 2a9 ffed b2 2a9 2a9 b5 ffeb ffeb b8 ffef 2a9 bb 2a9
  //   ffeb be 2a9 2a9 c1 ffeb 2a9 c4 2a9 ffeb c7 2a9 2a9 ca d1 d1 cd d0 d0 d2 0 0 2af 2a9 d5 2a9 d0 e7 2a9
  //   2a9 db 2ac d0 de ffeb 2a9 e1 2a9 d1 e4 2a9 2a9 d5 ffeb ffeb ea d1 2a9 ed 2a9 ffeb f0 2a9 2a9 f3 ffee
  //   2a9 f6 2a9 ffeb f9 2a9 2a9 fc ffeb 2a9 ff 2a9 ffeb 102 2a9 2a9 105 ffeb 2a9 108 2a9 ffeb 10b 2a9 2a9
  //   10e 115 115 111 114 114 116 0 0 2b0 2a9 119 2a9 114 12b 2a9 2a9 11f 2ac 114 122 ffeb 2a9 125 2a9 115
  //   128 2a9 2a9 119 ffeb ffeb 12e 115 2a9 131 2a9 ffeb 134 2a9 2a9 137 ffeb ffed 13a 13d 13d 13e 0 2aa
  //   ffed 141 2aa 13d 144 2b1 ffed 14a 2a9 2a9 141 ffed ffed 14d 13d 2a9 150 2a9 ffed 153 2a9 2a9 156 2ac
  //   ffed 159 ffec ffec 15c 2b2 2a9 15f 2a9 ffec 162 2a9 2a9 165 ffeb ffeb 168 ffef 2a9 16b 2a9 ffeb 16e
  //   2a9 2a9 171 ffeb 2a9 174 2a9 ffeb 177 2a9 2a9 17a 181 181 17d 180 180 182 0 0 2af 2a9 185 2a9 180
  //   197 2a9 2a9 18b 2ac 180 18e ffeb 2a9 191 2a9 181 194 2a9 2a9 185 ffeb ffeb 19a 181 2a9 19d 2a9 ffeb
  //   1a0 2a9 2a9 1a3 ffee 2a9 1a6 2a9 ffeb 1a9 2a9 2a9 1ac ffeb 2a9 1af 2a9 ffeb 1b2 2a9 2a9 1b5 1bc 1bc
  //   1b8 1bb 1bb 1bd 0 0 2af 2a9 1c0 2a9 1bb 1d2 2a9 2a9 1c6 2ac 1bb 1c9 ffeb 2a9 1cc 2a9 1bc 1cf 2a9 2a9
  //   1c0 ffeb ffeb 1d5 1bc 2a9 1d8 2a9 ffeb 1db 2a9 2a9 1de ffed 2a9 1e1 2a9 ffeb 1e4 2a9 2a9 1e7 ffeb
  //   2a9 1ea 2a9 ffeb 1ed 2a9 2a9 1f0 1f7 1f7 1f3 1f6 1f6 1f8 0 0 2af 2a9 1fb 2a9 1f6 20d 2a9 2a9 201 2ac
  //   1f6 204 ffeb 2a9 207 2a9 1f7 20a 2a9 2a9 1fb ffeb ffeb 210 1f7 2a9 213 2a9 ffeb 216 2a9 2a9 219 ffeb
  //   ffec 21c ffef 2a9 21f 2a9 ffef 222 2a9 2a9 225 ffef 2a9 228 2a9 ffef 22b 2a9 2a9 22e ffef 2a9 231
  //   2a9 ffef 234 2a9 2a9 237 ffef 2a9 23a 2a9 ffef 23d 2a9 2a9 240 ffee 2a9 243 2a9 ffef 246 2a9 2a9 249
  //   ffef 2a9 24c 2a9 ffef 24f 2a9 2a9 252 ffef 2a9 255 2a9 ffef 258 2a9 2a9 25b ffef 2a9 25e 2a9 ffef
  //   261 2a9 2a9 264 ffef 2a9 267 2a9 ffef 26a 2a9 2a9 26d ffed 2a9 270 2a9 ffef 273 2a9 2a9 276 ffef 2a9
  //   279 2a9 ffef 27c 2a9 2a9 27f ffef 2a9 282 2a9 ffef 285 2a9 2a9 288 ffef 2a9 28b 2a9 ffef 28e 2a9 2a9
  //   291 ffef 2a9 294 2a9 ffef 297 2a9 2a9 29a ffec 2a9 29d 2a9 ffef 2a0 2a9 2a9 2a3 ffef ffff 2a6 2a9
  //   2a9 2a6 0 ffff 3e8 1 7d 64 5 19 a 88b
endmodule
