// Logisim project slqisc_out.circ as structural Verilog: 1 circuit, main circuit main
module main (
  input  [6:0] labin
);

  wire and_1_out, and_2_out, and_3_out, and_4_out, and_5_out, and_6_out, and_7_out, and_8_out, and_9_out,
       and_10_out, and_11_out, and_12_out, and_13_out, and_14_out, and_15_out, and_16_out, and_17_out,
       and_18_out, and_19_out, and_20_out, and_21_out, and_22_out, and_23_out, and_24_out, and_25_out,
       and_26_out, and_27_out, and_28_out, and_29_out, and_30_out, and_31_out, and_32_out, and_33_out,
       and_34_out, and_35_out, and_36_out, and_37_out, and_38_out, and_39_out, and_40_out, and_41_out,
       and_42_out, and_43_out, and_44_out, and_45_out, and_46_out, and_47_out, and_48_out, and_49_out,
       and_50_out, and_51_out, and_52_out, and_53_out, and_54_out, and_55_out, and_56_out, and_57_out,
       and_58_out, and_59_out, and_60_out, and_61_out, and_62_out, and_63_out, and_64_out, and_65_out,
       and_66_out, and_67_out, and_68_out, and_69_out, and_70_out, and_71_out, and_72_out, and_73_out,
       and_74_out, and_75_out, and_76_out, and_77_out, and_78_out, and_79_out, and_80_out, and_81_out,
       and_82_out, and_83_out, and_84_out, and_85_out, and_86_out, and_87_out, and_88_out, and_89_out,
       and_90_out, and_91_out, and_92_out, and_93_out, and_94_out, and_95_out, and_96_out, and_97_out,
       and_98_out, and_99_out, and_100_out, and_101_out, and_102_out, and_103_out, and_104_out, and_105_out,
       and_106_out, and_107_out, and_108_out, and_109_out, and_110_out, and_111_out, and_112_out,
       and_113_out, and_114_out, and_115_out, and_116_out, and_117_out, and_118_out, and_119_out,
       and_120_out, and_121_out, and_122_out, and_123_out, and_124_out, and_125_out, and_126_out,
       and_127_out, and_128_out, and_129_out, and_130_out, and_131_out, and_132_out, and_133_out,
       and_134_out, and_135_out, and_136_out, and_137_out, and_138_out, and_139_out, and_140_out,
       and_141_out, and_142_out, and_143_out, and_144_out, and_145_out, and_146_out, and_147_out,
       and_148_out, and_149_out, and_150_out, and_151_out, and_152_out, and_153_out, and_154_out,
       and_155_out, and_156_out, and_157_out, and_158_out, and_159_out, and_160_out, and_161_out,
       and_162_out, and_163_out, and_164_out, and_165_out, and_166_out, and_167_out, and_168_out,
       and_169_out, and_170_out, and_171_out, and_172_out, and_173_out, and_174_out, and_175_out,
       and_176_out, and_177_out, and_178_out, and_179_out, and_180_out, and_181_out, and_182_out,
       and_183_out, and_184_out, and_185_out, and_186_out, and_187_out, and_188_out, and_189_out,
       and_190_out, and_191_out, and_192_out, and_193_out, and_194_out, and_195_out, and_196_out,
       and_197_out, and_198_out, and_199_out, and_200_out, and_201_out, and_202_out, and_203_out,
       and_204_out, and_205_out, and_206_out, and_207_out, and_208_out, and_209_out, and_210_out,
       and_211_out, and_212_out, and_213_out, and_214_out, and_215_out, and_216_out, and_217_out,
       and_218_out, and_219_out, and_220_out, and_221_out, and_222_out, and_223_out, and_224_out,
       and_225_out, and_226_out, and_227_out, and_228_out, and_229_out, and_230_out, and_231_out,
       and_232_out, and_233_out, and_234_out, and_235_out, and_236_out, and_237_out, and_238_out,
       and_239_out, and_240_out, and_241_out, not_1_out, not_2_out, not_3_out, not_4_out, not_5_out,
       not_6_out;
  wire [4:0] or_10_out, or_15_out, or_17_out, or_20_out, or_22_out;

  not not_1 (not_1_out, labin[5]);
  not not_2 (not_2_out, labin[4]);
  not not_3 (not_3_out, labin[3]);
  not not_4 (not_4_out, labin[2]);
  not not_5 (not_5_out, labin[1]);
  not not_6 (not_6_out, labin[0]);
  and and_1 (and_1_out, not_1_out, not_3_out, labin[1]);
  and and_2 (and_2_out, not_1_out, not_2_out, labin[1], labin[0]);
  and and_3 (and_3_out, not_1_out, not_2_out, labin[2]);
  and and_4 (and_4_out, not_3_out, not_4_out, labin[0]);
  and and_5 (and_5_out, not_3_out, labin[1], labin[0]);
  and and_6 (and_6_out, not_1_out, labin[3], not_4_out, not_5_out, not_6_out);
  and and_7 (and_7_out, not_1_out, labin[4], not_3_out);
  and and_8 (and_8_out, not_1_out, labin[4], not_4_out, not_5_out);
  and and_9 (and_9_out, not_1_out, labin[4], not_4_out, not_6_out);
  and and_10 (and_10_out, not_2_out, labin[3], labin[2], not_5_out, labin[0]);
  and and_11 (and_11_out, not_2_out, labin[3], not_5_out, not_6_out);
  and and_12 (and_12_out, not_1_out, labin[4], not_3_out, not_4_out);
  and and_13 (and_13_out, labin[4], not_4_out, not_5_out, labin[0]);
  and and_14 (and_14_out, not_3_out, not_5_out, labin[0]);
  and and_15 (and_15_out, not_3_out, labin[2], labin[0]);
  and and_16 (and_16_out, not_1_out, labin[3], labin[2], not_6_out);
  and and_17 (and_17_out, not_1_out, labin[2], labin[1]);
  and and_18 (and_18_out, not_2_out, labin[2], not_5_out);
  and and_19 (and_19_out, not_1_out, not_3_out, labin[1]);
  and and_20 (and_20_out, labin[5], not_4_out, labin[1], not_6_out);
  and and_21 (and_21_out, not_2_out, labin[3], not_4_out, labin[1], labin[0]);
  and and_22 (and_22_out, not_1_out, not_2_out, labin[2]);
  and and_23 (and_23_out, not_1_out, labin[4], not_3_out, not_4_out);
  and and_24 (and_24_out, labin[4], not_5_out, labin[0]);
  and and_25 (and_25_out, not_3_out, labin[2], labin[1], labin[0]);
  and and_26 (and_26_out, labin[3], labin[2], not_5_out, labin[0]);
  and and_27 (and_27_out, not_2_out, labin[3], not_4_out, not_6_out);
  and and_28 (and_28_out, not_1_out, not_3_out, labin[1]);
  and and_29 (and_29_out, not_2_out, labin[3], not_4_out, labin[1]);
  and and_30 (and_30_out, not_3_out, not_4_out, not_5_out, labin[0]);
  and and_31 (and_31_out, labin[5], not_2_out, not_4_out, not_6_out);
  and and_32 (and_32_out, not_1_out, labin[3], labin[2], not_5_out);
  and and_33 (and_33_out, labin[2], labin[1], labin[0]);
  and and_34 (and_34_out, not_1_out, not_3_out, not_5_out, labin[0]);
  and and_35 (and_35_out, not_1_out, labin[3], labin[2], not_5_out, not_6_out);
  and and_36 (and_36_out, not_2_out, not_3_out, labin[2], not_6_out);
  and and_37 (and_37_out, not_1_out, not_2_out, labin[1]);
  and and_38 (and_38_out, not_1_out, labin[4], not_3_out, not_4_out, not_6_out);
  and and_39 (and_39_out, not_2_out, labin[3], not_4_out, not_6_out);
  and and_40 (and_40_out, not_2_out, labin[3], labin[2], labin[0]);
  and and_41 (and_41_out, not_2_out, not_4_out, labin[1], not_6_out);
  and and_42 (and_42_out, labin[5], labin[3], not_4_out);
  and and_43 (and_43_out, not_1_out, not_2_out, labin[2]);
  and and_44 (and_44_out, not_3_out, not_4_out, not_5_out, labin[0]);
  and and_45 (and_45_out, not_3_out, labin[2], labin[1], labin[0]);
  and and_46 (and_46_out, not_1_out, labin[3], not_4_out, not_6_out);
  and and_47 (and_47_out, not_1_out, not_3_out, labin[0]);
  and and_48 (and_48_out, not_1_out, labin[3], labin[1], not_6_out);
  and and_49 (and_49_out, not_2_out, labin[3], not_4_out, labin[1], labin[0]);
  and and_50 (and_50_out, not_1_out, not_3_out, not_4_out, labin[1]);
  and and_51 (and_51_out, not_1_out, labin[4], not_4_out, not_6_out);
  and and_52 (and_52_out, not_2_out, labin[3], labin[2], not_5_out, labin[0]);
  and and_53 (and_53_out, labin[5], not_4_out, labin[1]);
  and and_54 (and_54_out, labin[5], labin[3], not_5_out, not_6_out);
  and and_55 (and_55_out, not_1_out, labin[4], not_3_out, not_4_out);
  and and_56 (and_56_out, not_2_out, not_3_out, not_5_out, labin[0]);
  and and_57 (and_57_out, not_2_out, not_3_out, labin[2], not_6_out);
  and and_58 (and_58_out, not_1_out, not_2_out, not_3_out, labin[1]);
  and and_59 (and_59_out, labin[4], labin[2], not_5_out, not_6_out);
  and and_60 (and_60_out, labin[4], labin[3], labin[1], not_6_out);
  and and_61 (and_61_out, not_1_out, labin[3], labin[2], labin[1], labin[0]);
  and and_62 (and_62_out, labin[5], not_2_out, not_3_out, not_4_out, not_5_out, not_6_out);
  and and_63 (and_63_out, labin[4], labin[3], not_4_out, not_5_out, not_6_out);
  and and_64 (and_64_out, not_1_out, labin[3], labin[2], not_5_out, labin[0]);
  and and_65 (and_65_out, not_1_out, not_2_out, labin[3], labin[2], labin[1], not_6_out);
  and and_66 (and_66_out, not_2_out, not_3_out, not_5_out, labin[0]);
  and and_67 (and_67_out, not_2_out, not_3_out, labin[1], not_6_out);
  and and_68 (and_68_out, labin[5], not_3_out, labin[2]);
  and and_69 (and_69_out, not_1_out, not_2_out, labin[3], not_4_out, not_5_out, not_6_out);
  and and_70 (and_70_out, not_2_out, labin[3], not_4_out, labin[1], labin[0]);
  and and_71 (and_71_out, labin[5], labin[2], not_5_out);
  and and_72 (and_72_out, not_1_out, labin[4], not_3_out, not_4_out, not_6_out);
  and and_73 (and_73_out, labin[4], not_3_out, not_4_out, labin[1]);
  and and_74 (and_74_out, labin[4], labin[3], not_4_out, not_5_out, labin[0]);
  and and_75 (and_75_out, labin[5], not_2_out, not_3_out, not_6_out);
  and and_76 (and_76_out, labin[5], labin[3], not_4_out, labin[1]);
  and and_77 (and_77_out, labin[5], not_5_out, labin[0]);
  and and_78 (and_78_out, labin[4], not_3_out, labin[2], labin[1]);
  and and_79 (and_79_out, labin[4], labin[3], not_4_out, not_6_out);
  and and_80 (and_80_out, labin[4], labin[2], labin[1], not_6_out);
  and and_81 (and_81_out, not_1_out, not_3_out, not_4_out, labin[1], labin[0]);
  and and_82 (and_82_out, not_2_out, not_3_out, labin[2], not_5_out);
  and and_83 (and_83_out, labin[4], not_3_out, not_5_out, labin[0]);
  and and_84 (and_84_out, labin[5], not_3_out, not_5_out, labin[0]);
  and and_85 (and_85_out, labin[5], not_3_out, labin[2]);
  and and_86 (and_86_out, labin[5], labin[3], not_4_out, not_5_out);
  and and_87 (and_87_out, not_2_out, not_4_out, labin[1], not_6_out);
  and and_88 (and_88_out, labin[3], labin[2], not_5_out, not_6_out);
  and and_89 (and_89_out, labin[4], labin[3], labin[1], not_6_out);
  and and_90 (and_90_out, not_2_out, labin[2], labin[1], labin[0]);
  and and_91 (and_91_out, labin[4], labin[3], labin[2], labin[1]);
  and and_92 (and_92_out, not_1_out, not_2_out, not_4_out, not_5_out, labin[0]);
  and and_93 (and_93_out, labin[4], labin[3], labin[2]);
  and and_94 (and_94_out, labin[5], not_6_out);
  and and_95 (and_95_out, labin[5], not_4_out, labin[1]);
  and and_96 (and_96_out, not_1_out, not_2_out, labin[2], labin[1], labin[0]);
  and and_97 (and_97_out, labin[4], not_4_out, labin[1]);
  and and_98 (and_98_out, not_1_out, not_2_out, not_3_out, labin[1]);
  and and_99 (and_99_out, labin[4], not_3_out, not_4_out);
  and and_100 (and_100_out, not_3_out, labin[2], not_5_out, not_6_out);
  and and_101 (and_101_out, not_2_out, not_3_out, not_5_out, labin[0]);
  and and_102 (and_102_out, labin[5], labin[4]);
  and and_103 (and_103_out, labin[4], not_3_out, labin[2], not_5_out, not_6_out);
  and and_104 (and_104_out, not_1_out, not_2_out, labin[3], not_4_out, not_5_out, labin[0]);
  and and_105 (and_105_out, labin[4], labin[3], not_4_out, labin[1], labin[0]);
  and and_106 (and_106_out, labin[4], labin[3], labin[2], not_5_out, labin[0]);
  and and_107 (and_107_out, not_1_out, labin[3], not_4_out, not_5_out);
  and and_108 (and_108_out, labin[3], not_4_out, labin[0]);
  and and_109 (and_109_out, labin[4], not_5_out, not_6_out);
  and and_110 (and_110_out, labin[5], not_3_out);
  and and_111 (and_111_out, labin[5], labin[1], not_6_out);
  and and_112 (and_112_out, labin[5], labin[2], not_5_out);
  and and_113 (and_113_out, not_3_out, not_4_out, labin[1], not_6_out);
  and and_114 (and_114_out, not_3_out, labin[2], labin[1], labin[0]);
  and and_115 (and_115_out, labin[4], not_4_out);
  and and_116 (and_116_out, not_2_out, not_5_out, labin[0]);
  and and_117 (and_117_out, not_2_out, labin[2], labin[1], not_6_out);
  and and_118 (and_118_out, labin[4], labin[3]);
  and and_119 (and_119_out, labin[5], labin[4]);
  and and_120 (and_120_out, labin[5], not_3_out, not_4_out, labin[1], labin[0]);
  and and_121 (and_121_out, labin[4], not_3_out, labin[2], not_5_out, not_6_out);
  and and_122 (and_122_out, not_1_out, labin[3], not_4_out, not_5_out, labin[0]);
  and and_123 (and_123_out, labin[4], labin[3], not_5_out, labin[0]);
  and and_124 (and_124_out, labin[5], labin[3], labin[2], labin[1], not_6_out);
  and and_125 (and_125_out, labin[3], not_4_out, not_5_out, labin[0]);
  and and_126 (and_126_out, labin[2], not_5_out, not_6_out);
  and and_127 (and_127_out, labin[4], labin[2], not_6_out);
  and and_128 (and_128_out, labin[5], labin[4]);
  and and_129 (and_129_out, labin[5], not_3_out, labin[0]);
  and and_130 (and_130_out, labin[5], labin[3], not_6_out);
  and and_131 (and_131_out, not_3_out, not_4_out, labin[1], labin[0]);
  and and_132 (and_132_out, not_3_out, labin[2], not_5_out);
  and and_133 (and_133_out, not_2_out, not_4_out, labin[1], not_6_out);
  and and_134 (and_134_out, labin[4], not_5_out, labin[0]);
  and and_135 (and_135_out, labin[5], labin[1], not_6_out);
  and and_136 (and_136_out, not_2_out, labin[2], labin[1], labin[0]);
  and and_137 (and_137_out, labin[4], labin[3], labin[1]);
  and and_138 (and_138_out, labin[5], not_4_out, labin[1]);
  and and_139 (and_139_out, labin[5], not_2_out, not_5_out, not_6_out);
  and and_140 (and_140_out, not_1_out, labin[4], not_3_out, not_4_out);
  and and_141 (and_141_out, not_2_out, not_3_out, not_5_out, labin[0]);
  and and_142 (and_142_out, not_2_out, not_3_out, labin[2], not_6_out);
  and and_143 (and_143_out, not_1_out, not_2_out, not_3_out, labin[1]);
  and and_144 (and_144_out, labin[4], labin[2], not_5_out, not_6_out);
  and and_145 (and_145_out, labin[4], labin[3], labin[1], not_6_out);
  and and_146 (and_146_out, not_1_out, labin[3], labin[2], labin[1], labin[0]);
  and and_147 (and_147_out, labin[5], not_2_out, not_3_out, not_4_out, not_5_out, not_6_out);
  and and_148 (and_148_out, labin[5], not_3_out, not_4_out, labin[1], labin[0]);
  and and_149 (and_149_out, labin[4], labin[3], not_4_out, not_6_out);
  and and_150 (and_150_out, not_1_out, not_2_out, labin[3], not_4_out, labin[1], labin[0]);
  and and_151 (and_151_out, not_1_out, not_2_out, labin[3], labin[2], not_5_out, labin[0]);
  and and_152 (and_152_out, not_2_out, not_3_out, not_5_out, labin[0]);
  and and_153 (and_153_out, not_1_out, not_2_out, labin[3], not_4_out, not_5_out, not_6_out);
  and and_154 (and_154_out, labin[5], not_5_out, labin[0]);
  and and_155 (and_155_out, labin[5], not_4_out, labin[1], not_6_out);
  and and_156 (and_156_out, labin[5], labin[2], not_5_out);
  and and_157 (and_157_out, not_1_out, labin[4], not_3_out, not_4_out, not_6_out);
  and and_158 (and_158_out, labin[4], not_3_out, not_4_out, labin[1]);
  and and_159 (and_159_out, labin[4], labin[3], not_4_out, not_5_out, labin[0]);
  and and_160 (and_160_out, labin[4], labin[3], labin[2], labin[1]);
  and and_161 (and_161_out, labin[5], not_2_out, not_3_out, not_6_out);
  and and_162 (and_162_out, not_2_out, not_3_out, labin[1], not_6_out);
  and and_163 (and_163_out, not_2_out, not_3_out, labin[2], labin[1]);
  and and_164 (and_164_out, labin[5], not_3_out, not_4_out, not_5_out, not_6_out);
  and and_165 (and_165_out, labin[4], not_3_out, not_4_out, not_5_out, labin[0]);
  and and_166 (and_166_out, labin[4], not_3_out, labin[1], not_6_out);
  and and_167 (and_167_out, labin[4], not_3_out, labin[2], labin[1]);
  and and_168 (and_168_out, labin[4], labin[3], not_4_out, not_5_out, not_6_out);
  and and_169 (and_169_out, not_1_out, not_2_out, labin[3], not_4_out, labin[1], labin[0]);
  and and_170 (and_170_out, not_1_out, not_2_out, labin[3], labin[2], labin[1], not_6_out);
  and and_171 (and_171_out, labin[5], not_2_out, not_4_out, not_5_out);
  and and_172 (and_172_out, not_1_out, not_3_out, not_4_out, labin[1], labin[0]);
  and and_173 (and_173_out, not_2_out, not_3_out, labin[2], not_5_out);
  and and_174 (and_174_out, labin[4], not_3_out, not_5_out, labin[0]);
  and and_175 (and_175_out, labin[5], not_3_out, labin[2]);
  and and_176 (and_176_out, not_2_out, not_4_out, labin[1], not_6_out);
  and and_177 (and_177_out, labin[3], not_4_out, labin[1], not_6_out);
  and and_178 (and_178_out, labin[3], labin[2], not_5_out, not_6_out);
  and and_179 (and_179_out, not_2_out, labin[2], labin[1], labin[0]);
  and and_180 (and_180_out, labin[4], labin[3], labin[2], labin[1]);
  and and_181 (and_181_out, not_1_out, not_2_out, labin[1]);
  and and_182 (and_182_out, not_1_out, not_2_out, labin[2], labin[0]);
  and and_183 (and_183_out, not_3_out, not_4_out, labin[0]);
  and and_184 (and_184_out, labin[5], labin[3], not_5_out, not_6_out);
  and and_185 (and_185_out, not_1_out, labin[3], not_4_out, not_6_out);
  and and_186 (and_186_out, not_1_out, labin[4], not_3_out);
  and and_187 (and_187_out, not_1_out, labin[4], not_4_out, not_5_out);
  and and_188 (and_188_out, labin[5], labin[3], not_4_out, not_5_out);
  and and_189 (and_189_out, not_2_out, labin[3], labin[2], labin[1], labin[0]);
  and and_190 (and_190_out, not_1_out, not_3_out, not_4_out, not_5_out, labin[0]);
  and and_191 (and_191_out, not_2_out, not_3_out, labin[2], not_5_out, not_6_out);
  and and_192 (and_192_out, not_1_out, not_2_out, labin[3], not_4_out, not_6_out);
  and and_193 (and_193_out, not_1_out, not_2_out, labin[3], labin[2], labin[0]);
  and and_194 (and_194_out, labin[4], not_4_out, not_5_out, labin[0]);
  and and_195 (and_195_out, labin[4], labin[3], labin[2], not_6_out);
  and and_196 (and_196_out, labin[5], not_3_out, labin[2], not_5_out);
  and and_197 (and_197_out, labin[5], not_3_out, labin[2], not_6_out);
  and and_198 (and_198_out, labin[5], labin[3], not_4_out, labin[0]);
  and and_199 (and_199_out, labin[5], labin[2], not_5_out, not_6_out);
  and and_200 (and_200_out, not_1_out, not_3_out, not_4_out, labin[1], not_6_out);
  and and_201 (and_201_out, not_1_out, labin[3], labin[2], labin[1]);
  and and_202 (and_202_out, not_1_out, labin[4], not_3_out, not_4_out, not_6_out);
  and and_203 (and_203_out, labin[4], not_3_out, labin[2], labin[0]);
  and and_204 (and_204_out, labin[5], labin[3], not_4_out, labin[1]);
  and and_205 (and_205_out, labin[4], labin[2], labin[1]);
  and and_206 (and_206_out, not_1_out, not_3_out, not_5_out, labin[0]);
  and and_207 (and_207_out, not_1_out, not_2_out, not_3_out, labin[2]);
  and and_208 (and_208_out, not_1_out, not_2_out, labin[3], not_4_out, not_6_out);
  and and_209 (and_209_out, not_1_out, not_2_out, labin[2], labin[0]);
  and and_210 (and_210_out, labin[4], not_3_out, not_4_out);
  and and_211 (and_211_out, labin[4], not_4_out, not_5_out, labin[0]);
  and and_212 (and_212_out, labin[4], labin[3], labin[2], not_5_out, not_6_out);
  and and_213 (and_213_out, labin[5], not_3_out, not_4_out, not_5_out, not_6_out);
  and and_214 (and_214_out, not_3_out, labin[2], not_5_out, labin[0]);
  and and_215 (and_215_out, not_3_out, labin[2], labin[1], not_6_out);
  and and_216 (and_216_out, labin[5], labin[3], not_4_out, not_5_out, labin[0]);
  and and_217 (and_217_out, labin[5], labin[3], labin[2], not_5_out, not_6_out);
  and and_218 (and_218_out, labin[4], not_3_out, labin[1]);
  and and_219 (and_219_out, not_2_out, labin[3], not_4_out, labin[1], not_6_out);
  and and_220 (and_220_out, not_1_out, not_2_out, labin[2], labin[1]);
  and and_221 (and_221_out, labin[5], labin[3], labin[2], labin[1], labin[0]);
  and and_222 (and_222_out, not_3_out, not_4_out, not_5_out, labin[0]);
  and and_223 (and_223_out, not_2_out, not_3_out, labin[2], not_5_out, not_6_out);
  and and_224 (and_224_out, labin[2], labin[1], labin[0]);
  and and_225 (and_225_out, not_1_out, not_2_out, labin[3], not_4_out, not_6_out);
  and and_226 (and_226_out, not_2_out, labin[3], labin[2], labin[0]);
  and and_227 (and_227_out, labin[4], not_3_out, labin[0]);
  and and_228 (and_228_out, labin[4], labin[3], labin[2], not_5_out, not_6_out);
  and and_229 (and_229_out, labin[5], not_5_out, labin[0]);
  and and_230 (and_230_out, labin[5], labin[2], not_5_out);
  and and_231 (and_231_out, not_2_out, not_3_out, not_4_out, labin[1], not_6_out);
  and and_232 (and_232_out, labin[5], not_3_out, labin[1], not_6_out);
  and and_233 (and_233_out, not_1_out, not_2_out, labin[3], labin[1], not_6_out);
  and and_234 (and_234_out, not_1_out, not_3_out, labin[0]);
  and and_235 (and_235_out, labin[5], labin[4]);
  and and_236 (and_236_out, not_1_out, not_4_out, labin[1], not_6_out);
  and and_237 (and_237_out, not_1_out, labin[3], labin[1], not_6_out);
  and and_238 (and_238_out, not_1_out, not_2_out, labin[3], labin[1]);
  and and_239 (and_239_out, labin[3], not_4_out, not_5_out, not_6_out);
  and and_240 (and_240_out, labin[5], labin[3], not_5_out, labin[0]);
  and and_241 (and_241_out, not_1_out, not_2_out, labin[3], labin[2]);
  or or_1 (or_17_out[4], and_53_out, and_54_out, and_55_out, and_56_out, and_57_out, and_58_out, and_59_out, and_60_out, and_61_out);
  or or_2 (or_17_out[3], and_62_out, and_63_out, and_64_out, and_65_out);
  or or_3 (or_17_out[1], and_78_out, and_79_out, and_80_out);
  or or_4 (or_20_out[3], and_102_out, and_103_out, and_104_out, and_105_out, and_106_out);
  or or_5 (or_20_out[1], and_119_out, and_120_out, and_121_out, and_122_out, and_123_out, and_124_out);
  or or_6 (or_22_out[4], and_138_out, and_139_out, and_140_out, and_141_out, and_142_out, and_143_out, and_144_out, and_145_out, and_146_out);
  or or_7 (or_22_out[3], and_147_out, and_148_out, and_149_out, and_150_out, and_151_out);
  or or_8 (or_22_out[1], and_164_out, and_165_out, and_166_out, and_167_out, and_168_out, and_169_out, and_170_out);
  or or_9 (or_10_out[4], and_181_out, and_182_out, and_183_out, and_184_out, and_185_out, and_186_out, and_187_out, and_188_out, and_189_out);
  or or_10 (or_10_out[0], and_234_out, and_235_out, and_236_out, and_237_out, and_238_out, and_239_out, and_240_out, and_241_out);
  or or_11 (or_15_out[4], and_1_out, and_2_out, and_3_out, and_4_out, and_5_out, and_6_out, and_7_out, and_8_out, and_9_out, and_10_out);
  or or_12 (or_15_out[3], and_11_out, and_12_out, and_13_out, and_14_out, and_15_out, and_16_out, and_17_out, and_18_out, and_19_out, and_20_out, and_21_out);
  or or_13 (or_15_out[2], and_22_out, and_23_out, and_24_out, and_25_out, and_26_out, and_27_out, and_28_out, and_29_out, and_30_out, and_31_out, and_32_out);
  or or_14 (or_15_out[1], and_33_out, and_34_out, and_35_out, and_36_out, and_37_out, and_38_out, and_39_out, and_40_out, and_41_out, and_42_out);
  or or_15 (or_15_out[0], and_43_out, and_44_out, and_45_out, and_46_out, and_47_out, and_48_out, and_49_out, and_50_out, and_51_out, and_52_out);
  or or_16 (or_17_out[2], and_66_out, and_67_out, and_68_out, and_69_out, and_70_out, and_71_out, and_72_out, and_73_out, and_74_out, and_75_out, and_76_out, and_77_out);
  or or_17 (or_17_out[0], and_81_out, and_82_out, and_83_out, and_84_out, and_85_out, and_86_out, and_87_out, and_88_out, and_89_out, and_90_out, and_91_out);
  or or_18 (or_20_out[4], and_92_out, and_93_out, and_94_out, and_95_out, and_96_out, and_97_out, and_98_out, and_99_out, and_100_out, and_101_out);
  or or_19 (or_20_out[2], and_107_out, and_108_out, and_109_out, and_110_out, and_111_out, and_112_out, and_113_out, and_114_out, and_115_out, and_116_out, and_117_out, and_118_out);
  or or_20 (or_20_out[0], and_125_out, and_126_out, and_127_out, and_128_out, and_129_out, and_130_out, and_131_out, and_132_out, and_133_out, and_134_out, and_135_out, and_136_out, and_137_out);
  or or_21 (or_22_out[2], and_152_out, and_153_out, and_154_out, and_155_out, and_156_out, and_157_out, and_158_out, and_159_out, and_160_out, and_161_out, and_162_out, and_163_out);
  or or_22 (or_22_out[0], and_171_out, and_172_out, and_173_out, and_174_out, and_175_out, and_176_out, and_177_out, and_178_out, and_179_out, and_180_out);
  or or_23 (or_10_out[3], and_190_out, and_191_out, and_192_out, and_193_out, and_194_out, and_195_out, and_196_out, and_197_out, and_198_out, and_199_out, and_200_out, and_201_out, and_202_out, and_203_out, and_204_out, and_205_out);
  or or_24 (or_10_out[2], and_206_out, and_207_out, and_208_out, and_209_out, and_210_out, and_211_out, and_212_out, and_213_out, and_214_out, and_215_out, and_216_out, and_217_out, and_218_out, and_219_out, and_220_out, and_221_out);
  or or_25 (or_10_out[1], and_222_out, and_223_out, and_224_out, and_225_out, and_226_out, and_227_out, and_228_out, and_229_out, and_230_out, and_231_out, and_232_out, and_233_out);
  DotMatrix #(.matrixrows(5)) dotmatrix_1 (
    .col0(or_15_out), .col1(or_17_out), .col2(or_20_out), .col3(or_22_out), .col4(or_10_out));
endmodule
